# Fritzing sketch Rocket_Lander_Rev1 (saved by Fritzing 0.9.2b)
breadboards: 2

parts:
  U20 = Arduino Uno (Rev3)
  U22 = Grove 4 Digit Display
  U7 = Adafruit Arcade Joystick
  M4_(SE) = Stepper Motor - Bipolar
  M3_(SW) = Stepper Motor - Bipolar
  M2_(NE) = Stepper Motor - Bipolar
  M1_(NW) = Stepper Motor - Bipolar
  U24 = Intel Edison Arduinobreakout
  U21 = Grove 4 Digit Display
  U6 = SLIDER [package=slider]
  U2 = Grove OLED 128x96
  U5 = Basic Servo
  U4 = Basic Servo
  U12 = DIP - 14 pins [chip_label=74LS00 package="DIP (Dual Inline) [THT]"]
  U11 = DIP - 14 pins [chip_label=74LS00 package="DIP (Dual Inline) [THT]"]
  U16 = DIP - 20 pins [part_number="Adafruit TB6612 Stepper Motor Driver" chip_label=TB6612 package="DIP (Dual Inline) [THT]"]
  U15 = DIP - 20 pins [part_number="Adafruit TB6612 Stepper Motor Driver" chip_label=TB6612 package="DIP (Dual Inline) [THT]"]
  U14 = DIP - 20 pins [part_number="Adafruit TB6612 Stepper Motor Driver" chip_label=TB6612 package="DIP (Dual Inline) [THT]"]
  U13 = DIP - 20 pins [part_number="Adafruit TB6612 Stepper Motor Driver" chip_label=TB6612 package="DIP (Dual Inline) [THT]"]
  J10 = Power Jack [package=power_jack_pth]
  R7 = Resistor [tolerance=±5% resistance=220 package=THT]
  R8 = Resistor [tolerance=±5% resistance=220 package=THT]
  U25 = DIP - 16 pins [chip_label=74LS138 package="DIP (Dual Inline) [THT]"]
  U26 = DIP - 28 pins [chip_label="Audio FX Sound Board" package="DIP (Dual Inline) [THT]"]
  R5 = Resistor [tolerance=±5% resistance=22k package=THT]
  R6 = Resistor [tolerance=±5% resistance=10k package=THT]
  R4 = Resistor [tolerance=±5% resistance=22k package=THT]
  R3 = Resistor [tolerance=±5% resistance=10k package=THT]
  R1 = Resistor [tolerance=±5% resistance=47k package=THT]
  R2 = Resistor [tolerance=±5% resistance=47k package=THT]
  U23 = Grove Chainable RGB LED
  J20 = 2.5mm Audio Jack [package=stereojack2.5mm_smd]
  U9 = Arcade Button (red)
  U8 = Arcade Button (green) [part_number="Button 1"]
  C10 = Electrolytic Capacitor [capacitance=0.1mF voltage=50V package="100 mil [THT, electrolytic]"]
  C11 = Electrolytic Capacitor [capacitance=0.1mF voltage=50V package="100 mil [THT, electrolytic]"]
  C12 = Electrolytic Capacitor [capacitance=0.1mF voltage=50V package="100 mil [THT, electrolytic]"]
  C13 = Electrolytic Capacitor [capacitance=0.1mF voltage=50V package="100 mil [THT, electrolytic]"]
  R10 = Resistor [tolerance=±5% resistance=470 package=THT]
  LED1 = LED - 5mm [color="Red (633nm)" package="5 mm [THT]"]
  U1 = Intel Galileo Gen2
  U3 = 1.2" 7-segment 4-digit Backpack [part_number="Adafruit 1.2\" 4-Digit 7-Segment Display"]
  U10 = Arduino Micro (Rev3)

nets:
  N1: U20.A2, U23.CLK
  N2: U20.A3, U23.DI
  N3: U20.D8, U22.DIO
  N4: U20.D9_PWM, U25.A0
  N5: U20.D10_PWM/SS, U25.A1
  N6: U20.D11_PWM/MOSI, U25.A2
  GND: U20.GND, U22.GND, U24.GND, U21.GND, U6.A, U2.GND, U5.gnd, U4.gnd, U12.GND, U11.GND, U16.GND#12, U15.GND#12, U14.GND#12, U13.GND#12, U25.~E1, U25.~E2, U25.GND, U26.GND, R1.Pin_0, R2.Pin_0, U23.GND, J20.SLEEVE, U9.no_name_yet#1, U8.no_name_yet#1, R10.Pin_0, U1.GND, U3.GND, U10.GND
  N7: U20.A4/SDA, U2.SCL, U1.A5/SCL, U3.SCL, U10.D2/SDA
  N8: U20.A5/SCL, U2.SDA, U1.A4/SDA, U3.SDA, U10.D3/SCL
  N9: U20.D3_PWM, U24.D1/TX
  N10: U20.D4, U24.D0/RX
  N11: U20.D5_PWM, U21.CLK
  N12: U20.D6_PWM, U21.DIO
  N13: U20.D7, U22.CLK
  VCC: U20.5V, U22.VCC, U21.VCC, U25.E3, U25.VCC, U26.Vin, U23.VCC
  VCC_2: U7.COM, U6.E, U2.VCC, U5.vcc, U4.vcc, R7.Pin_0, R8.Pin_0, U1.5V, U3.IO, U3.V+
  N14: U7.N, R3.Pin_0
  N15: U7.S, R4.Pin_0
  N16: U7.W, R5.Pin_0
  N17: U7.E, R6.Pin_0
  N18: M4_(SE).A, U13.B2
  N19: M4_(SE).C, U13.B1
  N20: M4_(SE).B, U13.A2
  N21: M4_(SE).D, U13.A1
  N22: M3_(SW).A, U14.B2
  N23: M3_(SW).C, U14.B1
  N24: M3_(SW).B, U14.A2
  N25: M3_(SW).D, U14.A1
  N26: M2_(NE).A, U15.B2
  N27: M2_(NE).C, U15.B1
  N28: M2_(NE).B, U15.A2
  N29: M2_(NE).D, U15.A1
  N30: M1_(NW).A, U16.B2
  N31: M1_(NW).C, U16.B1
  N32: M1_(NW).B, U16.A2
  N33: M1_(NW).D, U16.A1
  N34: U6.S, U1.A2
  N35: U5.pulse, U1.D6_PWM
  N36: U4.pulse, U1.D5_PWM
  N37: U12.1A, U12.1B, U16.AIN1, U10.D4_PWM/A6
  N38: U12.1Y, U16.AIN2
  N39: U12.2A, U12.2B, U16.BIN1, U10.D5_PWM
  N40: U12.2Y, U16.BIN2
  N41: U12.3Y, U15.AIN2
  N42: U12.3A, U12.3B, U15.AIN1, U10.D6_PWM/A7
  N43: U12.4Y, U15.BIN2
  N44: U12.4A, U12.4B, U15.BIN1, U10.D7
  VCC_3: U12.VCC, U11.VCC, U16.VCC, U15.VCC, U14.VCC, U13.VCC, U10.5V
  N45: U11.1A, U11.1B, U14.AIN1, U10.D8_PWM/A8
  N46: U11.1Y, U14.AIN2
  N47: U11.2A, U11.2B, U14.BIN1, U10.D9_PWM/A9
  N48: U11.2Y, U14.BIN2
  N49: U11.3Y, U13.AIN2
  N50: U11.3A, U11.3B, U13.AIN1, U10.D10_PWM/A10
  N51: U11.4Y, U13.BIN2
  N52: U11.4A, U11.4B, U13.BIN1, U10.D11_PWM
  N53: U16.GND#4, U16.GND#5, U15.GND#4, U15.GND#5, U14.GND#4, U14.GND#5, U13.GND#4, U13.GND#5, J10.GND, C10.-, C11.-, C12.-, C13.-
  N54: U16.VM, U15.VM, U14.VM, U13.VM, J10.PWR, C10.+, C11.+, C12.+, C13.+
  N55: U16.STBY, U15.STBY, U14.STBY, U13.STBY, LED1.cathode, U10.D12_PWM/A11
  N56: R7.Pin_1, U9.no_name_yet#2, U1.D7
  N57: R8.Pin_1, U8.no_name_yet#2, U1.D3_PWM
  N58: U25.~Y7, U26.7
  N59: U25.~Y6, U26.6
  N60: U25.~Y5, U26.5
  N61: U25.~Y4, U26.4
  N62: U25.~Y3, U26.3
  N63: U25.~Y2, U26.2
  N64: U25.~Y1, U26.1
  N65: U25.~Y0, U26.0
  N66: U26.L, J20.LEFT
  N67: U26.R, J20.RIGHT
  N68: R5.Pin_1, R6.Pin_1, R2.Pin_1, U1.A0
  N69: R4.Pin_1, R3.Pin_1, R1.Pin_1, U1.A1
  N70: R10.Pin_1, LED1.anode

notes:
  +12 Volts, 5 Amps
  Rocket Control
  Rocket Display
  Rocket Motor
  Rocket Lander
  ========================
  Version 1: Four Motor System
  May 2016

custom parts:
  DIP - 14 pins: A DIP stand-in part for whatever IC you want. With 14 pins on a 300mil dual inline package (DIP) footprint.
  DIP - 20 pins: A DIP stand-in part for whatever IC you want. With 20 pins on a 600mil dual inline package (DIP) footprint.
  DIP - 16 pins: A DIP stand-in part for whatever IC you want. With 16 pins on a 300mil dual inline package (DIP) footprint.
  DIP - 28 pins: A DIP stand-in part for whatever IC you want. With 28 pins on a 600mil dual inline package (DIP) footprint.
  Grove Chainable RGB LED: A chainable RGB LED
  Arcade Button (red): Adafruit Arcade Button (red)
  Arcade Button (green): Adafruit Arcade Button (green)
  1.2" 7-segment 4-digit Backpack: Adafruit 1.2" 4-Digit 7-Segment Display w/I2C Backpack - Red[ID:1270]
